# Fritzing sketch circuit (saved by Fritzing 0.9.3b)

parts:
  WeMos_D1_Mini1 = WeMos D1 Mini
  HC-SR04_Sensor_1 = HC-SR04 Ultrasonic Distance Sensor
  M1 = DC Motor  # not connected
  Power_plug1 = Power plug  # not connected

nets:
  5V: WeMos_D1_Mini1.5V, HC-SR04_Sensor_1.VCC
  N1: WeMos_D1_Mini1.D6, HC-SR04_Sensor_1.TRIG
  N2: WeMos_D1_Mini1.D7, HC-SR04_Sensor_1.ECHO
  N3: WeMos_D1_Mini1.G, HC-SR04_Sensor_1.GND
